# Fritzing sketch project keyless wiring diagram fritzing (saved by Fritzing 0.9.9b)
breadboards: 1

parts:
  Part2 = RFID-RC522-v2
  Part1 = Arduino Uno (Rev3) - ICSP
  Part3 = Jtron 1 Channel Optoisolated Relay Module [package=relay]
  Part4 = LCD1602-I2C

nets:
  N1: Part2.SDA, Part1.D10_PWM/SS
  N2: Part2.SCK, Part1.D13/SCK
  N3: Part2.MOSI, Part1.D11_PWM/MOSI
  N4: Part2.MISO, Part1.D12/MISO
  GND: Part2.GND, Part1.GND, Part3.GND, Part4.GND
  N5: Part2.RST, Part1.D9_PWM
  3.3V: Part2.3.3V, Part1.3V3
  N6: Part1.A4/SDA, Part4.SDA
  N7: Part1.A5/SCL, Part4.SCL
  N8: Part1.D8, Part3.IN1
  5V: Part1.5V, Part4.VCC

notes:
  LCD+I2C
  GND>GND
  VCC>+5V
  SDA>A4
  SCL>A5
  RELAY 1CH ACTIV LOW
  VCC>+5V
  GND>GND
  IN>8

custom parts:
  RFID-RC522-v2: A simple China made RFID-RC522 Reader; do check the pin labels, as this is a MFRC522 based clone.
  LCD1602-I2C: A standard character display, usually with 2x16 characters. Comes in many colors with LCM1602 IIC attached.
